// Logisim project gpu.circ as structural Verilog: 1 circuit, main circuit main
module main (
);

  wire and_1_out, and_2_out, and_3_out, button_1_out, clock_1_out, comparator_1_eq, comparator_2_eq,
       comparator_3_eq, comparator_4_gt, comparator_5_lt, comparator_6_lt, comparator_7_lt,
       demultiplexer_1_out0, demultiplexer_1_out1, demultiplexer_1_out2, demultiplexer_1_out3,
       demultiplexer_1_out4, demultiplexer_1_out5, demultiplexer_1_out6, demultiplexer_1_out7,
       demultiplexer_1_out8, nor_1_out, not_1_out, or_1_out;
  wire [1:0] register_8_q_2, register_9_q_2, register_10_q_2;
  wire [3:0] divider_1_rem;
  wire [7:0] counter_2_q, divider_1_out, register_8_q, register_9_q, register_10_q, subtractor_1_out;
  wire [7:4] divider_1_rem_2;
  wire [9:0] bit_extender_1_out, bit_extender_2_out, bit_extender_3_out, register_1_q, register_2_q,
       register_3_q, register_4_q, register_5_q, register_6_q, register_7_q, rom_1_data, subtractor_2_out,
       subtractor_3_out, subtractor_4_out, subtractor_5_out, subtractor_6_out, subtractor_7_out,
       subtractor_8_out, subtractor_9_out, subtractor_10_out, subtractor_11_out, subtractor_12_out,
       subtractor_13_out;
  wire [13:0] counter_1_q;
  wire [15:0] bit_extender_4_out, bit_extender_5_out, bit_extender_6_out, bit_extender_7_out,
       bit_extender_8_out, bit_extender_9_out, bit_extender_10_out, bit_extender_11_out, bit_extender_12_out,
       bit_extender_13_out, bit_extender_14_out, bit_extender_15_out, multiplier_1_out, multiplier_2_out,
       multiplier_3_out, multiplier_4_out, multiplier_5_out, multiplier_6_out, subtractor_14_out,
       subtractor_15_out, subtractor_16_out;
  wire [23:0] multiplexer_1_out, multiplexer_2_out, register_11_q;

  Button button_1 (.out(button_1_out));
  Clock clock_1 (.out(clock_1_out));
  ROM #(.dataWidth(10)) rom_1 (.addr(counter_2_q), .data(rom_1_data));
  Counter #(.max('h3fff), .width(14)) counter_1 (
    .count(and_1_out), .Q(counter_1_q), .clk(clock_1_out), .clr(button_1_out));  // open: load, D, carry
  Counter counter_2 (
    .load(and_1_out), .D({8{1'b0}}), .count(1'b1), .Q(counter_2_q), .clk(clock_1_out), .clr(button_1_out));  // open: carry
  Subtractor subtractor_1 (.a(counter_2_q), .b(8'h1), .out(subtractor_1_out));  // open: bin, bout
  Divider divider_1 (
    .a(subtractor_1_out), .b(8'h9), .out(divider_1_out), .rem({divider_1_rem_2, divider_1_rem}));  // open: upper
  Demultiplexer #(.enable("false"), .select(4)) demultiplexer_1 (
    .out0(demultiplexer_1_out0), .out1(demultiplexer_1_out1), .out2(demultiplexer_1_out2),
    .out3(demultiplexer_1_out3), .out4(demultiplexer_1_out4), .out5(demultiplexer_1_out5),
    .out6(demultiplexer_1_out6), .out7(demultiplexer_1_out7), .out8(demultiplexer_1_out8), .sel(divider_1_rem));  // open: out9, out10, out11, out12, out13, out14, out15, in
  Comparator #(.mode("unsigned"), .width(10)) comparator_1 (
    .a(register_1_q), .b(bit_extender_1_out), .eq(comparator_1_eq));  // open: gt, lt
  assign bit_extender_1_out = {{2{1'b0}}, divider_1_out};  // Bit_Extender bit_extender_1
  Register #(.width(10)) register_1 (
    .D(rom_1_data), .en(comparator_2_eq), .Q(register_1_q), .clk(clock_1_out));  // open: clr
  Comparator #(.mode("unsigned")) comparator_2 (.a(counter_2_q), .b({8{1'b0}}), .eq(comparator_2_eq));  // open: gt, lt
  not not_1 (not_1_out, comparator_2_eq);
  and and_1 (and_1_out, not_1_out, comparator_1_eq);
  Register #(.width(10)) register_2 (
    .D(rom_1_data), .en(demultiplexer_1_out0), .Q(register_2_q), .clk(clock_1_out));  // open: clr
  // Probe on counter_1_q[6:0]
  Register #(.width(10)) register_3 (
    .D(rom_1_data), .en(demultiplexer_1_out1), .Q(register_3_q), .clk(clock_1_out));  // open: clr
  // Probe on counter_1_q[13:7]
  Register #(.width(10)) register_4 (
    .D(rom_1_data), .en(demultiplexer_1_out2), .Q(register_4_q), .clk(clock_1_out));  // open: clr
  Register #(.width(10)) register_5 (
    .D(rom_1_data), .en(demultiplexer_1_out3), .Q(register_5_q), .clk(clock_1_out));  // open: clr
  // Probe on {register_10_q, register_9_q, register_8_q}
  Comparator #(.mode("unsigned")) comparator_3 (
    .a({8{1'b0}}), .b({divider_1_rem_2, divider_1_rem}), .eq(comparator_3_eq));  // open: gt, lt
  Register #(.width(10)) register_6 (
    .D(rom_1_data), .en(demultiplexer_1_out4), .Q(register_6_q), .clk(clock_1_out));  // open: clr
  assign bit_extender_2_out = {{3{1'b0}}, counter_1_q[6:0]};  // Bit_Extender bit_extender_2
  assign bit_extender_3_out = {{3{1'b0}}, counter_1_q[13:7]};  // Bit_Extender bit_extender_3
  Comparator #(.mode("unsigned"), .width(10)) comparator_4 (
    .a(bit_extender_1_out), .b({10{1'b0}}), .gt(comparator_4_gt));  // open: eq, lt
  Register #(.width(10)) register_7 (
    .D(rom_1_data), .en(demultiplexer_1_out5), .Q(register_7_q), .clk(clock_1_out));  // open: clr
  and and_2 (and_2_out, comparator_3_eq, comparator_4_gt);
  Register #(.width(10)) register_8 (
    .D(rom_1_data), .en(demultiplexer_1_out6), .Q({register_8_q_2, register_8_q}), .clk(clock_1_out));  // open: clr
  Register #(.width(10)) register_9 (
    .D(rom_1_data), .en(demultiplexer_1_out7), .Q({register_9_q_2, register_9_q}), .clk(clock_1_out));  // open: clr
  Subtractor #(.width(10)) subtractor_2 (
    .a(bit_extender_2_out), .b(register_2_q), .out(subtractor_2_out));  // open: bin, bout
  Subtractor #(.width(10)) subtractor_3 (
    .a(bit_extender_2_out), .b(register_4_q), .out(subtractor_3_out));  // open: bin, bout
  Subtractor #(.width(10)) subtractor_4 (
    .a(bit_extender_3_out), .b(register_3_q), .out(subtractor_4_out));  // open: bin, bout
  Subtractor #(.width(10)) subtractor_5 (
    .a(bit_extender_3_out), .b(register_5_q), .out(subtractor_5_out));  // open: bin, bout
  Subtractor #(.width(10)) subtractor_6 (
    .a(register_2_q), .b(register_6_q), .out(subtractor_6_out));  // open: bin, bout
  Subtractor #(.width(10)) subtractor_7 (
    .a(register_4_q), .b(register_2_q), .out(subtractor_7_out));  // open: bin, bout
  Subtractor #(.width(10)) subtractor_8 (
    .a(register_3_q), .b(register_7_q), .out(subtractor_8_out));  // open: bin, bout
  Subtractor #(.width(10)) subtractor_9 (
    .a(register_5_q), .b(register_3_q), .out(subtractor_9_out));  // open: bin, bout
  Register #(.width(10)) register_10 (
    .D(rom_1_data), .en(demultiplexer_1_out8), .Q({register_10_q_2, register_10_q}), .clk(clock_1_out));  // open: clr
  Subtractor #(.width(10)) subtractor_10 (
    .a(bit_extender_2_out), .b(register_6_q), .out(subtractor_10_out));  // open: bin, bout
  Subtractor #(.width(10)) subtractor_11 (
    .a(bit_extender_3_out), .b(register_7_q), .out(subtractor_11_out));  // open: bin, bout
  Subtractor #(.width(10)) subtractor_12 (
    .a(register_6_q), .b(register_4_q), .out(subtractor_12_out));  // open: bin, bout
  Subtractor #(.width(10)) subtractor_13 (
    .a(register_7_q), .b(register_5_q), .out(subtractor_13_out));  // open: bin, bout
  assign bit_extender_4_out = {{6{subtractor_10_out[9]}}, subtractor_10_out};  // Bit_Extender bit_extender_4
  assign bit_extender_5_out = {{6{subtractor_2_out[9]}}, subtractor_2_out};  // Bit_Extender bit_extender_5
  assign bit_extender_6_out = {{6{subtractor_5_out[9]}}, subtractor_5_out};  // Bit_Extender bit_extender_6
  assign bit_extender_7_out = {{6{subtractor_12_out[9]}}, subtractor_12_out};  // Bit_Extender bit_extender_7
  assign bit_extender_8_out = {{6{subtractor_6_out[9]}}, subtractor_6_out};  // Bit_Extender bit_extender_8
  assign bit_extender_9_out = {{6{subtractor_9_out[9]}}, subtractor_9_out};  // Bit_Extender bit_extender_9
  assign bit_extender_10_out = {{6{subtractor_3_out[9]}}, subtractor_3_out};  // Bit_Extender bit_extender_10
  assign bit_extender_11_out = {{6{subtractor_11_out[9]}}, subtractor_11_out};  // Bit_Extender bit_extender_11
  assign bit_extender_12_out = {{6{subtractor_4_out[9]}}, subtractor_4_out};  // Bit_Extender bit_extender_12
  assign bit_extender_13_out = {{6{subtractor_7_out[9]}}, subtractor_7_out};  // Bit_Extender bit_extender_13
  assign bit_extender_14_out = {{6{subtractor_13_out[9]}}, subtractor_13_out};  // Bit_Extender bit_extender_14
  assign bit_extender_15_out = {{6{subtractor_8_out[9]}}, subtractor_8_out};  // Bit_Extender bit_extender_15
  Multiplier #(.width(16)) multiplier_1 (
    .a(bit_extender_5_out), .b(bit_extender_9_out), .out(multiplier_1_out));  // open: cin, cout
  Multiplier #(.width(16)) multiplier_2 (
    .a(bit_extender_12_out), .b(bit_extender_13_out), .out(multiplier_2_out));  // open: cin, cout
  Multiplier #(.width(16)) multiplier_3 (
    .a(bit_extender_10_out), .b(bit_extender_14_out), .out(multiplier_3_out));  // open: cin, cout
  Multiplier #(.width(16)) multiplier_4 (
    .a(bit_extender_6_out), .b(bit_extender_7_out), .out(multiplier_4_out));  // open: cin, cout
  Multiplier #(.width(16)) multiplier_5 (
    .a(bit_extender_4_out), .b(bit_extender_15_out), .out(multiplier_5_out));  // open: cin, cout
  Multiplier #(.width(16)) multiplier_6 (
    .a(bit_extender_11_out), .b(bit_extender_8_out), .out(multiplier_6_out));  // open: cin, cout
  Subtractor #(.width(16)) subtractor_14 (
    .a(multiplier_1_out), .b(multiplier_2_out), .out(subtractor_14_out));  // open: bin, bout
  Subtractor #(.width(16)) subtractor_15 (
    .a(multiplier_3_out), .b(multiplier_4_out), .out(subtractor_15_out));  // open: bin, bout
  Subtractor #(.width(16)) subtractor_16 (
    .a(multiplier_5_out), .b(multiplier_6_out), .out(subtractor_16_out));  // open: bin, bout
  Comparator #(.width(16)) comparator_5 (.a(subtractor_14_out), .b({16{1'b0}}), .lt(comparator_5_lt));  // open: gt, eq
  Comparator #(.width(16)) comparator_6 (.a(subtractor_15_out), .b({16{1'b0}}), .lt(comparator_6_lt));  // open: gt, eq
  nor nor_1 (nor_1_out, comparator_7_lt, comparator_6_lt, comparator_5_lt);
  Comparator #(.width(16)) comparator_7 (.a(subtractor_16_out), .b({16{1'b0}}), .lt(comparator_7_lt));  // open: gt, eq
  and and_3 (and_3_out, and_2_out, nor_1_out);
  Multiplexer #(.enable("false"), .width(24)) multiplexer_1 (
    .in0({register_10_q, register_9_q, register_8_q}), .in1({24{1'b0}}), .out(multiplexer_1_out),
    .sel(and_1_out));
  or or_1 (or_1_out, and_3_out, and_1_out);
  Register #(.width(24)) register_11 (
    .D(multiplexer_1_out), .en(or_1_out), .Q(register_11_q), .clk(clock_1_out));  // open: clr
  Multiplexer #(.enable("false"), .width(24)) multiplexer_2 (
    .in0(register_11_q), .in1({register_10_q, register_9_q, register_8_q}), .out(multiplexer_2_out),
    .sel(and_3_out));
  // RGB_Video rgb_video_1: pin names not known; wires that end beside it: button_1_out, clock_1_out, and_1_out, counter_1_q[6:0], counter_1_q[13:7], multiplexer_2_out

  // Notes on the sheet:
  //   contents of rom_1 (hex, n*v repeats v):
  //   3 8 5 10 42 70 65 4d 3c f3 8 5 70 65 50 30 f3 3c 4d 10 42 5 75 70 65 4d f3 3c
  //   TRIANGLE BUFFER
  //   Y
  //   X
  //   X
  //   P
  //   Y
  //   X
  //   V0
  //   Y
  //   X
  //   V1
  //   Y
  //   X
  //   V2
  //   Y
  //   Color
  //   Tri Ready
  //   i
  //   e
  //   a
  //   k
  //   g
  //   c
  //   h
  //   d
  //   l
  //   f
  //   b
  //   j
  //   TRIANGLE RASTERIZER
  //   m
  //   n
  //   o
  //   p
  //   q
  //   r
  //   s
  //   t
  //   u
endmodule
